# Fritzing sketch Drone Turret + Controller Wiring Diagram (saved by Fritzing 1.0.6)
breadboards: 1

parts:
  Part1 = Arduino Uno (Rev3)
  Adafruit_TMC2209_Stepper_Motor_Driver1 = Adafruit TMC2209 Stepper Motor Driver [part_number=#6121]
  M1 = Stepper Motor - Bipolar  # not connected
  J1 = Basic Servo

nets:
  N1: Part1.D9_PWM, J1.pulse
  GND: Part1.GND, Adafruit_TMC2209_Stepper_Motor_Driver1.GND
  N2: Part1.D3_PWM, Adafruit_TMC2209_Stepper_Motor_Driver1.STEP
  N3: Part1.D4, Adafruit_TMC2209_Stepper_Motor_Driver1.DIR
  N4: Part1.D5_PWM, Adafruit_TMC2209_Stepper_Motor_Driver1.ENABLE
  3V3: Part1.3V3, Adafruit_TMC2209_Stepper_Motor_Driver1.VDD

notes:
  12V Power Supply
  12V to 7.4V
